// Logisim project Ctl_Data_Processing.circ as structural Verilog: 1 circuit, main circuit Data_Processing
module Data_Processing (
  input  Enable,
  input  [15:0] Instruction,
  output [2:0] Rd,
  output [2:0] Rn,
  output [2:0] Rm,
  output [3:0] ALU_Opcode,
  output [3:0] Flags_Update_Mask
);

  wire and_1_out, and_2_out, and_3_out, and_5_out, not_1_out, not_3_out, RM_SELECT, RN_SELECT;
  wire [1:0] FLAG_OUT;
  wire [2:0] RM_OUT, RN_OUT;

  Multiplexer #(.select(4)) multiplexer_1 (
    .in0(1'b0), .in1(1'b0), .in2(1'b0), .in3(1'b0), .in4(1'b0), .in5(1'b1), .in6(1'b1), .in7(1'b0),
    .in8(1'b0), .in9(1'b1), .in10(1'b1), .in11(1'b1), .in12(1'b0), .in13(1'b0), .in14(1'b0), .in15(1'b0),
    .out(FLAG_OUT[0]), .sel(Instruction[9:6]));  // open: en
  and and_1 (and_1_out, Instruction[6], ~Instruction[7], ~Instruction[8], Instruction[9]);  // AND_Gate
  and and_2 (and_2_out, Instruction[6], Instruction[7], ~Instruction[8], Instruction[9]);  // AND_Gate
  and and_3 (and_3_out, Instruction[6], ~Instruction[7], Instruction[8], Instruction[9]);  // AND_Gate
  and and_4 (RN_SELECT, and_1_out, and_2_out);
  assign RN_OUT = RN_SELECT ? Instruction[5:3] : 3'bz;  // Controlled_Buffer controlled_buffer_1
  assign RN_OUT = not_1_out ? Instruction[2:0] : 3'bz;  // Controlled_Buffer controlled_buffer_2
  not not_1 (not_1_out, RN_SELECT);
  and and_5 (and_5_out, and_3_out, Instruction[8]);
  not not_2 (FLAG_OUT[1], and_5_out);
  assign RM_OUT = RM_SELECT ? Instruction[2:0] : 3'bz;  // Controlled_Buffer controlled_buffer_3
  assign RM_OUT = not_3_out ? Instruction[5:3] : 3'bz;  // Controlled_Buffer controlled_buffer_4
  not not_3 (not_3_out, RM_SELECT);
  Pull_Resistor pull_resistor_1 (.node(Rd));
  assign Rd = Enable ? Instruction[2:0] : 3'bz;  // Controlled_Buffer controlled_buffer_5
  Pull_Resistor pull_resistor_2 (.node(Rn));
  assign Rn = Enable ? RN_OUT : 3'bz;  // Controlled_Buffer controlled_buffer_6
  Pull_Resistor pull_resistor_3 (.node(Rm));
  assign Rm = Enable ? RM_OUT : 3'bz;  // Controlled_Buffer controlled_buffer_7
  Pull_Resistor pull_resistor_4 (.node(ALU_Opcode));
  assign ALU_Opcode = Enable ? Instruction[9:6] : 4'bz;  // Controlled_Buffer controlled_buffer_8
  Pull_Resistor pull_resistor_5 (.node(Flags_Update_Mask));
  assign Flags_Update_Mask = Enable ? {2'b11, FLAG_OUT} : 4'bz;  // Controlled_Buffer controlled_buffer_9
  and and_6 (RM_SELECT, Instruction[6], Instruction[7], ~Instruction[8], Instruction[9]);  // AND_Gate

  // Other names for the same wires on the sheet: INS1[2:0] = Instruction[2:0]; RD_OUT[2:0] = Instruction[2:0];
  //   INS2[2:0] = Instruction[5:3]; ALU_OUT[3:0] = Instruction[9:6]

  // Notes on the sheet:
  //   Note 2: RSB instruction has Rn as 1st operand.
  //   MUL instruction has Rn as 1st operand and Rdm as 2nd operand
  //   For simplification purposes, Rm is used for 1st operand both here and in the ALU.
  //   Note: instructions that does not save the result will still have the second operand as the destination register, the ALU will copy the second register to the destination register
  //   Pull output low on Enable = 0
endmodule
