// Logisim project Ctl_Load_Store.circ as structural Verilog: 1 circuit, main circuit Load_Store
module Load_Store (
  input  [15:0] Instruction,
  input  Enable,
  input  Clk,
  input  Reset,
  input  [31:0] Stack_Pointer,
  output Store,
  output Load,
  output PC_Hold,
  output [2:0] Rmd,
  output [31:0] RAM_Addr
);

  wire and_1_out, and_2_out, and_3_out, d_ff_1_q, d_ff_1_qn, not_1_out, not_2_out, or_1_out, STORE_OR_LOAD;
  wire [31:0] adder_1_out, imm8_32;

  BitSelector #(.width(16)) bitselector_1 (.in(Instruction), .out(STORE_OR_LOAD), .sel(4'b1011));
  not not_1 (not_1_out, STORE_OR_LOAD);
  and and_1 (and_1_out, ~d_ff_1_q, STORE_OR_LOAD);  // AND_Gate
  not not_2 (not_2_out, Enable);
  Multiplexer #(.enable("false")) multiplexer_1 (.in0(1'b0), .in1(not_1_out), .out(Store), .sel(Enable));
  D_Flip_Flop #(.trigger("falling")) d_ff_1 (
    .D(and_1_out), .clk(Clk), .Q(d_ff_1_q), .Qn(d_ff_1_qn), .reset(or_1_out));  // open: preset
  or or_1 (or_1_out, Reset, not_2_out);
  and and_2 (and_2_out, d_ff_1_q, STORE_OR_LOAD);
  and and_3 (and_3_out, d_ff_1_qn, STORE_OR_LOAD);
  Multiplexer #(.enable("false")) multiplexer_2 (.in0(1'b0), .in1(and_3_out), .out(PC_Hold), .sel(Enable));
  Multiplexer #(.enable("false")) multiplexer_3 (.in0(1'b0), .in1(and_2_out), .out(Load), .sel(Enable));
  assign imm8_32 = {{24{Instruction[7]}}, Instruction[7:0]};  // Bit_Extender bit_extender_1
  Multiplexer #(.enable("false"), .width(3)) multiplexer_4 (
    .in0(3'b000), .in1(Instruction[10:8]), .out(Rmd), .sel(Enable));
  Adder #(.width(32)) adder_1 (.a(Stack_Pointer), .b(imm8_32), .out(adder_1_out));  // open: cin, cout
  Multiplexer #(.enable("false"), .width(32)) multiplexer_5 (
    .in0({32{1'b0}}), .in1(adder_1_out), .out(RAM_Addr), .sel(Enable));

  // Other names for the same wires on the sheet: HOLD = PC_Hold; RST = Reset; SP[31:0] = Stack_Pointer

  // Notes on the sheet:
  //   Instruction: pull=down
  //   Decode Instruction
  //   Processing
  //   Delay load and hold PC for 1 cycle for the RAM to send out requested data 
  //   RAM Adress Calculator
endmodule
