// Logisim project Ctl_Opcode_Decoder.circ as structural Verilog: 1 circuit, main circuit Opcode_Decoder
module Opcode_Decoder (
  input  [5:0] Opcode,
  output Shift,
  output Data_Processing,
  output Load_Store,
  output SP_Address,
  output Conditional
);

  wire and_4_out, and_5_out;

  and and_1 (Shift, ~Opcode[4], ~Opcode[5]);  // AND_Gate
  and and_2 (Load_Store, Opcode[2], ~Opcode[3], ~Opcode[4], Opcode[5]);  // AND_Gate
  and and_3 (SP_Address, Opcode[2], Opcode[3], ~Opcode[4], Opcode[5]);  // AND_Gate
  and and_4 (and_4_out, Opcode[2], ~Opcode[3], Opcode[4], Opcode[5]);  // AND_Gate
  and and_5 (and_5_out, ~Opcode[0], ~Opcode[1], Opcode[2], Opcode[3], Opcode[4], Opcode[5]);  // AND_Gate
  and and_6 (Data_Processing, ~Opcode[0], ~Opcode[1], ~Opcode[2], ~Opcode[3], Opcode[4], ~Opcode[5]);  // AND_Gate
  or or_1 (Conditional, and_4_out, and_5_out);

  // Other names for the same wires on the sheet: COND = Conditional; DP = Data_Processing; LS = Load_Store;
  //   OP_IN[5:0] = Opcode; SP = SP_Address

  // Notes on the sheet:
  //   Decoder
  //   Shift, add, sub, mov (00XXXX)
  //   Load/Store (1001XX)
  //   SP Address (1011XX)
  //   Data Processing (01000X)
  //   Conditional branch (1101 cond)(11100 uncond)
  //   Output
endmodule
