// Logisim project Ctl_SP_Address.circ as structural Verilog: 1 circuit, main circuit SP_Address
module SP_Address (
  input  [31:0] Stack_Pointer,
  input  [15:0] Instruction,
  input  Enable,
  output [31:0] New_Stack_Pointer,
  output Write_Enable
);

  wire ADD_OR_SUB;
  wire [31:0] adder_1_out, imm7_32, multiplexer_1_out, subtractor_1_out;

  BitSelector #(.width(16)) bitselector_1 (.in(Instruction), .out(ADD_OR_SUB), .sel(4'b0111));
  assign imm7_32 = {{25{1'b0}}, Instruction[6:0]};  // Bit_Extender bit_extender_1
  Adder #(.width(32)) adder_1 (.a(Stack_Pointer), .b(imm7_32), .out(adder_1_out));  // open: cin, cout
  Subtractor #(.width(32)) subtractor_1 (.a(Stack_Pointer), .b(imm7_32), .out(subtractor_1_out));  // open: bin, bout
  Multiplexer #(.enable("false"), .width(32)) multiplexer_1 (
    .in0(adder_1_out), .in1(subtractor_1_out), .out(multiplexer_1_out), .sel(ADD_OR_SUB));
  Multiplexer #(.enable("false"), .width(32)) multiplexer_2 (
    .in0({32{1'b0}}), .in1(multiplexer_1_out), .out(New_Stack_Pointer), .sel(Enable));

  assign Write_Enable = Enable;

  // Other names for the same wires on the sheet: SP[31:0] = Stack_Pointer

  // Notes on the sheet:
  //   Pull output low on Enable = 0
  //   Instruction Decoder
  //   Stack Pointer Calculation
endmodule
