// Logisim project Ctl_Shift_Add_Sub_Mov.circ as structural Verilog: 1 circuit, main circuit Shift_Add_Sub_Mov
module Shift_Add_Sub_Mov (
  input  Enable,
  input  [15:0] Instruction,
  output [3:0] Flags_Update_Mask,
  output Carry,
  output [2:0] Rm,
  output [2:0] Rn,
  output [2:0] Rd,
  output Imm32_Enable,
  output [31:0] Imm32,
  output [4:0] Imm5,
  output [3:0] ALU_Opcode
);

  wire ADD_8_EN, ADD_I_EN, ADD_R_EN, ASR_EN, CMP_EN, demultiplexer_1_out0, demultiplexer_1_out1,
       demultiplexer_1_out2, demultiplexer_1_out3, demultiplexer_1_out4, demultiplexer_1_out5,
       demultiplexer_1_out6, demultiplexer_1_out7, demultiplexer_1_out8, demultiplexer_1_out9,
       demultiplexer_1_out10, demultiplexer_1_out11, demultiplexer_1_out16, demultiplexer_1_out17,
       demultiplexer_1_out18, demultiplexer_1_out19, demultiplexer_1_out20, demultiplexer_1_out21,
       demultiplexer_1_out22, demultiplexer_1_out23, demultiplexer_1_out24, demultiplexer_1_out25,
       demultiplexer_1_out26, demultiplexer_1_out27, demultiplexer_1_out28, demultiplexer_1_out29,
       demultiplexer_1_out30, demultiplexer_1_out31, GLOB_EN, LSL_EN, LSR_EN, MOV_EN, SUB_8_EN, SUB_I_EN,
       SUB_R_EN;
  wire [3:3] NZC, NZCV;

  and and_1 (GLOB_EN, Instruction[14], Instruction[15]);
  Demultiplexer #(.enable("false"), .select(5)) demultiplexer_1 (
    .out0(demultiplexer_1_out0), .out1(demultiplexer_1_out1), .out2(demultiplexer_1_out2),
    .out3(demultiplexer_1_out3), .out4(demultiplexer_1_out4), .out5(demultiplexer_1_out5),
    .out6(demultiplexer_1_out6), .out7(demultiplexer_1_out7), .out8(demultiplexer_1_out8),
    .out9(demultiplexer_1_out9), .out10(demultiplexer_1_out10), .out11(demultiplexer_1_out11),
    .out12(ADD_R_EN), .out13(SUB_R_EN), .out14(ADD_I_EN), .out15(SUB_I_EN), .out16(demultiplexer_1_out16),
    .out17(demultiplexer_1_out17), .out18(demultiplexer_1_out18), .out19(demultiplexer_1_out19),
    .out20(demultiplexer_1_out20), .out21(demultiplexer_1_out21), .out22(demultiplexer_1_out22),
    .out23(demultiplexer_1_out23), .out24(demultiplexer_1_out24), .out25(demultiplexer_1_out25),
    .out26(demultiplexer_1_out26), .out27(demultiplexer_1_out27), .out28(demultiplexer_1_out28),
    .out29(demultiplexer_1_out29), .out30(demultiplexer_1_out30), .out31(demultiplexer_1_out31), .in(1'b1),
    .sel(Instruction[13:9]));
  or or_1 (LSL_EN, demultiplexer_1_out0, demultiplexer_1_out1, demultiplexer_1_out2, demultiplexer_1_out3);
  or or_2 (LSR_EN, demultiplexer_1_out4, demultiplexer_1_out5, demultiplexer_1_out6, demultiplexer_1_out7);
  or or_3 (ASR_EN, demultiplexer_1_out8, demultiplexer_1_out9, demultiplexer_1_out10, demultiplexer_1_out11);
  or or_4 (MOV_EN, demultiplexer_1_out16, demultiplexer_1_out17, demultiplexer_1_out18, demultiplexer_1_out19);
  or or_5 (CMP_EN, demultiplexer_1_out20, demultiplexer_1_out21, demultiplexer_1_out22, demultiplexer_1_out23);
  or or_6 (ADD_8_EN, demultiplexer_1_out24, demultiplexer_1_out25, demultiplexer_1_out26, demultiplexer_1_out27);
  or or_7 (SUB_8_EN, demultiplexer_1_out28, demultiplexer_1_out29, demultiplexer_1_out30, demultiplexer_1_out31);
  or or_8 (Carry, SUB_I_EN, SUB_8_EN, SUB_R_EN);
  or or_9 (Imm32_Enable, MOV_EN, CMP_EN, ADD_8_EN, SUB_8_EN, ADD_R_EN, SUB_R_EN, ADD_I_EN, SUB_I_EN);
  assign Flags_Update_Mask = {{3{NZC[3]}}, 1'b0} | {4{NZCV[3]}} | {{2{MOV_EN}}, 2'b00};  // OR_Gate or_10, 4 bits wide
  or or_11 (NZC[3], LSL_EN, LSR_EN, ASR_EN);
  or or_12 (NZCV[3], ADD_R_EN, SUB_R_EN, ADD_I_EN, SUB_I_EN, CMP_EN, ADD_8_EN, SUB_8_EN);

  assign Imm5 = Instruction[10:6];
  assign Rm = Instruction[5:3];

  // Other names for the same wires on the sheet: FUM[3:0] = Flags_Update_Mask; INS[15:0] = Instruction;
  //   NZ[3:2] = {2{MOV_EN}}; NZC[2:1] = {2{NZC[3]}}; NZCV[2:0] = {3{NZCV[3]}}

  // Notes on the sheet:
  //   Note: ALU uses Rn register for shifts. Use Rn instead of Rm for shifts (immediate) here too
  //   Note 3: Imm32_Enable forces the use of the immediate for Rm register
  //   Pull output low on Enable = 0
  //   Note 2: MOV uses RSB ALU opcode with Imm8 reversed so that it is copied to output register
  //   only ADD and SUB use Rm
  //   ALU will use Imm32 instead of Rm
  //   Seulement pour LSL, LSR, ASR
  //   NZ
  //   Enable carry for SUB since it is reversed in ALU
  //   NZC
  //   NZCV
endmodule
